# Fritzing sketch ocarina (saved by Fritzing 0.9.3b)
circuit board: 8.44787cm x 5.4941cm
breadboards: 1

parts:
  Teensy_4_0 = Teensy 3.1
  UDA1334 = Adafruit UDA1334 I2S DAC [part_number="Adafruit #3678"]
  Capacitive_Touch = Adafruit MPR121
  MPRLS = Adafruit MPRLS Sensor Breakout [part_number=3965]
  Powerboost_1000C = Adafruit PowerBoost 1000C with USB Port [part_number="Adafruit #2465"]
  S1 = Toggle Switch [package=THT]

nets:
  N1: Teensy_4_0.D7, UDA1334.DATA_IN
  N2: Teensy_4_0.A4/D18, Capacitive_Touch.SDA, MPRLS.SDA
  N3: Teensy_4_0.A5/D19, Capacitive_Touch.SCL, MPRLS.SCL
  N4: Teensy_4_0.A6/D20, UDA1334.WORDSEL_IN
  N5: Teensy_4_0.A7/D21, UDA1334.BITCLK_IN
  3V3: Teensy_4_0.3V3, MPRLS.VIN
  GND: Teensy_4_0.AGND, UDA1334.GND, Capacitive_Touch.GND, MPRLS.GND, Powerboost_1000C.GND, S1.L1
  VIN: Teensy_4_0.Vin, UDA1334.VIN, Capacitive_Touch.VIN, Powerboost_1000C.5.0V
  N6: Powerboost_1000C.ENABLE, S1.COM

notes:
  Electric Ocarina

custom parts:
  Adafruit UDA1334 I2S DAC: This fully-featured UDA1334A I2S Stereo DAC breakout is a perfect match for any I2S-output audio interface. It's affordable but sounds great! The NXP UDA1334A is a jack-of-all-I2S-trades: you can use 3.3V - 5V logic levels (a rarity), and can process multiple different formats by setting two pins to high or low. The DAC will process data immediately, and give you a clear, analog, stereo line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
  Adafruit MPR121: Add lots of touch sensors to your next microcontroller project with this easy-to-use 12-channel capacitive touch sensor breakout board, starring the MPR121. This chip can handle up to 12 individual touch pads. The MPR121 has support for only I2C, which can be implemented with nearly any microcontroller. You can select one of 4 addresses with the ADDR pin, for a total of 48 capacitive touch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
  Adafruit MPRLS Sensor Breakout: This pressure sensor is special because it comes with a metal port - you can easily attach a tube to it, to measure air pressure inside a close space. In particular we think this would be a great sensor for use with making DIY assistive tech "Sip & Puff" interfaces, or measuring the pressure within a vacuum chamber or other pressurized container. The port is made of stainless steel and is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
  Adafruit PowerBoost 1000C with USB Port: PowerBoost 1000C is the perfect power supply for your portable project! With a built-in load-sharing battery charger circuit, you'll be able to keep your power-hungry project running even while recharging the battery! This little DC/DC boost converter module can be powered by any 3.7V LiIon/LiPoly battery, and convert the battery output to 5.2V DC for running your 5V projects.
